// Logisim project My-PC.circ as structural Verilog
module and_or_latch (
  input  in_1,
  input  in_2,
  output out_3
);

  wire not_1_out, or_1_out;

  or or_1 (or_1_out, out_3, in_1);
  not not_1 (not_1_out, in_2);
  and and_1 (out_3, or_1_out, not_1_out);
endmodule

module gated_latch (
  input  in_1,
  input  in_2,
  output out_3
);

  wire and_1_out, and_2_out, not_1_out;

  and and_1 (and_1_out, in_1, in_2);
  not not_1 (not_1_out, in_1);
  and and_2 (and_2_out, not_1_out, in_2);
  and_or_latch and_or_latch_1 (.in_1(and_1_out), .in_2(and_2_out), .out_3(out_3));
endmodule
